# Fritzing sketch wemos-d1-rs323-converter-wiring (saved by Fritzing 0.9.3b)

parts:
  Bauteil1 = MAX3232
  WeMos_D1_Mini1 = WeMos D1 Mini
  S1 = Pushbutton [package="[THT]"]

nets:
  VCC: Bauteil1.VCC, WeMos_D1_Mini1.3V3
  N1: Bauteil1.RXD, WeMos_D1_Mini1.D5
  N2: Bauteil1.TXD, WeMos_D1_Mini1.D6
  N3: Bauteil1.GND, WeMos_D1_Mini1.G, S1.Pin_1, S1.Pin_2
  N4: WeMos_D1_Mini1.D7, S1.Pin_3

custom parts:
  MAX3232: A random MAX3232 Breakout Board from AliExpress (RS232-TTL-Converter)
